# Fritzing sketch LED Loading Bar (saved by Fritzing 0.9.3b)
breadboards: 1

parts:
  Part1 = Arduino Uno (Rev3)
  Red = LED - 5mm [color="Red (633nm)" package="5 mm [THT]"]
  Red_2 = LED - 5mm [color="Red (633nm)" package="5 mm [THT]"]
  Red_3 = LED - 5mm [color="Red (633nm)" package="5 mm [THT]"]
  Yellow = LED - 5mm [color="Yellow (585nm)" package="5 mm [THT]"]
  Yellow_2 = LED - 5mm [color="Yellow (585nm)" package="5 mm [THT]"]
  Yellow_3 = LED - 5mm [color="Yellow (585nm)" package="5 mm [THT]"]
  Green = LED - 5mm [color="Green (555nm)" package="5 mm [THT]"]
  Green_2 = LED - 5mm [color="Green (555nm)" package="5 mm [THT]"]
  Green_3 = LED - 5mm [color="Green (555nm)" package="5 mm [THT]"]
  R1 = Resistor [tolerance=±5% resistance=220 package=THT]
  R2 = Resistor [tolerance=±5% resistance=220 package=THT]
  R3 = Resistor [tolerance=±5% resistance=220 package=THT]
  R4 = Resistor [tolerance=±5% resistance=220 package=THT]
  R5 = Resistor [tolerance=±5% resistance=220 package=THT]
  R6 = Resistor [tolerance=±5% resistance=220 package=THT]
  R7 = Resistor [tolerance=±5% resistance=220 package=THT]
  R8 = Resistor [tolerance=±5% resistance=220 package=THT]
  R9 = Resistor [tolerance=±5% resistance=220 package=THT]

nets:
  N1: Part1.D8, R3.Pin_0
  N2: Part1.D9_PWM, R2.Pin_0
  N3: Part1.D10_PWM/SS, R1.Pin_0
  N4: Part1.D2, R9.Pin_0
  N5: Part1.D3_PWM, R8.Pin_0
  N6: Part1.D4, R7.Pin_0
  N7: Part1.D5_PWM, R6.Pin_0
  N8: Part1.D6_PWM, R5.Pin_0
  N9: Part1.D7, R4.Pin_0
  N10: Part1.GND, Red.cathode, Red_2.cathode, Red_3.cathode, Yellow.cathode, Yellow_2.cathode, Yellow_3.cathode, Green.cathode, Green_2.cathode, Green_3.cathode
  N11: Red.anode, R8.Pin_1
  N12: Red_2.anode, R7.Pin_1
  N13: Red_3.anode, R9.Pin_1
  N14: Yellow.anode, R6.Pin_1
  N15: Yellow_2.anode, R5.Pin_1
  N16: Yellow_3.anode, R4.Pin_1
  N17: Green.anode, R3.Pin_1
  N18: Green_2.anode, R2.Pin_1
  N19: Green_3.anode, R1.Pin_1
